# Fritzing sketch Magnetic-Stirrer-Fritzing (saved by Fritzing 0.9.3b)
breadboards: 1

parts:
  Power_plug_-_12V = Power plug
  R2_-_Resistor_for_LED = Resistor [tolerance=±5% resistance=470 package=THT]
  LED1 = LED - 5mm [color="Red (633nm)" package="5 mm [THT]"]
  M1_Fan = DC Motor
  S1_-_Power_Switch = Pushbutton [package=THT]
  R1_-_100_ohm_potmeter = Rotary Potentiometer (Small) [maximum_resistance=100Ω package=THT]
  R1 = Resistor [tolerance=±5% resistance=68 package=THT]
  S1 = Pushbutton [package=THT]
  R2 = Resistor [tolerance=±5% resistance=68 package=THT]
  S2 = Pushbutton [package=THT]
  R3 = Resistor [tolerance=±5% resistance=0 package=THT]

nets:
  N1: Power_plug_-_12V.GND, LED1.cathode, M1_Fan.pin_2, R1_-_100_ohm_potmeter.leg1, R3.Pin_0
  N2: Power_plug_-_12V.VCC, S1_-_Power_Switch.leg0, S1.leg0, S2.leg0
  N3: R2_-_Resistor_for_LED.Pin_0, M1_Fan.pin_1, R1_-_100_ohm_potmeter.wiper
  N4: R2_-_Resistor_for_LED.Pin_1, LED1.anode
  N5: S1_-_Power_Switch.leg1, R1_-_100_ohm_potmeter.leg2
  N6: R1.Pin_0, R2.Pin_0, R3.Pin_1
  N7: R1.Pin_1, S1.leg1
  N8: R2.Pin_1, S2.leg1

notes:
  12V power supply
  Fan
  Power switch
  Potmeter
  Indicator LED
